// Logisim project get_to_zero.circ as structural Verilog: 11 circuits, main circuit random_val_tb
module main (
  input  reset,
  input  state_1,
  input  state_2,
  input  state_3
);

  wire clock_1_out;
  wire [1:0] s;
  wire [7:0] a, blink_anim_1_hex0_out, blink_anim_1_hex1_out, blink_anim_1_hex2_out, blink_anim_1_hex3_out,
       blink_anim_1_hex4_out, blink_anim_1_hex5_out, e, g, m, multiplexer_1_out, multiplexer_2_out,
       multiplexer_3_out, multiplexer_4_out, multiplexer_5_out, multiplexer_6_out, r, s_letter,
       side_to_side_anim_1_hex0_out, side_to_side_anim_1_hex1_out, side_to_side_anim_1_hex2_out,
       side_to_side_anim_1_hex3_out, side_to_side_anim_1_hex4_out, side_to_side_anim_1_hex5_out, t;

  Clock #(.highDuration(12500000), .lowDuration(12500000)) clock_1 (.out(clock_1_out));
  letter_no_decimal letter_no_decimal_1 (.letter_num(5'b10011), .no_dec_letter(s_letter));
  letter_no_decimal letter_no_decimal_2 (.letter_num(5'b10100), .no_dec_letter(t));
  letter_no_decimal letter_no_decimal_3 (.letter_num(5'b00001), .no_dec_letter(a));
  letter_no_decimal letter_no_decimal_4 (.letter_num(5'b10010), .no_dec_letter(r));
  side_to_side_anim side_to_side_anim_1 (
    .clock(clock_1_out), .hex5_letter(s_letter), .hex4_letter(t), .hex3_letter(a), .hex2_letter(r),
    .hex1_letter(t), .hex5_out(side_to_side_anim_1_hex5_out), .hex4_out(side_to_side_anim_1_hex4_out),
    .hex3_out(side_to_side_anim_1_hex3_out), .hex2_out(side_to_side_anim_1_hex2_out),
    .hex1_out(side_to_side_anim_1_hex1_out), .hex0_out(side_to_side_anim_1_hex0_out));
  blink_anim blink_anim_1 (
    .clock(clock_1_out), .hex5_letter(g), .hex4_letter(a), .hex3_letter(m), .hex2_letter(e),
    .hex1_letter({8{1'b0}}), .hex0_letter({8{1'b0}}), .hex5_out(blink_anim_1_hex5_out),
    .hex4_out(blink_anim_1_hex4_out), .hex3_out(blink_anim_1_hex3_out), .hex2_out(blink_anim_1_hex2_out),
    .hex1_out(blink_anim_1_hex1_out), .hex0_out(blink_anim_1_hex0_out));
  letter_no_decimal letter_no_decimal_5 (.letter_num(5'b00111), .no_dec_letter(g));
  letter_no_decimal letter_no_decimal_6 (.letter_num(5'b01110), .no_dec_letter(m));
  letter_no_decimal letter_no_decimal_7 (.letter_num(5'b00101), .no_dec_letter(e));
  Multiplexer #(.select(2), .width(8)) multiplexer_1 (
    .in0(side_to_side_anim_1_hex5_out), .in1(blink_anim_1_hex5_out), .out(multiplexer_1_out), .sel(s));  // open: in2, in3
  Multiplexer #(.select(2), .width(8)) multiplexer_2 (
    .in0(side_to_side_anim_1_hex4_out), .in1(blink_anim_1_hex4_out), .out(multiplexer_2_out), .sel(s));  // open: in2, in3
  Multiplexer #(.select(2), .width(8)) multiplexer_3 (
    .in0(side_to_side_anim_1_hex3_out), .in1(blink_anim_1_hex3_out), .out(multiplexer_3_out), .sel(s));  // open: in2, in3
  Multiplexer #(.select(2), .width(8)) multiplexer_4 (
    .in0(side_to_side_anim_1_hex2_out), .in1(blink_anim_1_hex2_out), .out(multiplexer_4_out), .sel(s));  // open: in2, in3
  Multiplexer #(.select(2), .width(8)) multiplexer_5 (
    .in0(side_to_side_anim_1_hex1_out), .in1(blink_anim_1_hex1_out), .out(multiplexer_5_out), .sel(s));  // open: in2, in3
  Multiplexer #(.select(2), .width(8)) multiplexer_6 (
    .in0(side_to_side_anim_1_hex0_out), .in1(blink_anim_1_hex0_out), .out(multiplexer_6_out), .sel(s));  // open: in2, in3
  sevenseg_mapped hex5 (.sevenseg_input(multiplexer_1_out));
  sevenseg_mapped hex4 (.sevenseg_input(multiplexer_2_out));
  sevenseg_mapped hex3 (.sevenseg_input(multiplexer_3_out));
  sevenseg_mapped hex2 (.sevenseg_input(multiplexer_4_out));
  sevenseg_mapped hex1 (.sevenseg_input(multiplexer_5_out));
  sevenseg_mapped hex0 (.sevenseg_input(multiplexer_6_out));
  counter_fsm counter_fsm_1 (.reset(reset), .state_1(state_1), .state_2(state_2), .state_3(state_3), .state_output(s));
endmodule

module counter_fsm (
  input  reset,
  input  state_1,
  input  state_2,
  input  state_3,
  output [1:0] state_output
);

  wire and_1_out, and_2_out, and_3_out, comparator_1_eq, comparator_2_eq, comparator_3_eq, or_1_out;

  Comparator #(.mode("unsigned"), .width(2)) comparator_1 (
    .a(state_output), .b(2'b00), .eq(comparator_1_eq));  // open: gt, lt
  Comparator #(.mode("unsigned"), .width(2)) comparator_2 (
    .a(state_output), .b(2'b01), .eq(comparator_2_eq));  // open: gt, lt
  Comparator #(.mode("unsigned"), .width(2)) comparator_3 (
    .a(state_output), .b(2'b10), .eq(comparator_3_eq));  // open: gt, lt
  and and_1 (and_1_out, comparator_1_eq, state_1);
  and and_2 (and_2_out, state_2, comparator_2_eq);
  and and_3 (and_3_out, state_3, comparator_3_eq);
  or or_1 (or_1_out, and_1_out, and_2_out, and_3_out);
  Counter #(.max('h3), .width(2)) counter_1 (
    .clr(reset), .up(1'b1), .count(1'b1), .clk(or_1_out), .Q(state_output));  // open: load, D, carry
endmodule

module game_logic_tb (
  input  button,
  input  reset,
  input  miso,
  input  accel_input,
  output mosi,
  output sclk,
  output cs,
  output done
);

  wire absolute_val_and_sign_1_negative, and_1_out, clock_1_out, clock_2_out, comparator_1_eq,
       comparator_2_eq, comparator_3_eq, d_ff_2_q, d_ff_3_q, debouce_3_debouced, init_reset, or_1_out,
       or_2_out, or_3_out, play, reset_t;
  wire [3:0] hex_to_decimal_16_bits_1_ones, hex_to_decimal_16_bits_1_tens;
  wire [7:0] save_random_val_1_final_random_val, save_random_val_2_final_random_val;
  wire [15:0] absolute_val_and_sign_1_value, accel_final_driver_v2_1_x_filtered, adder_1_out,
       multiplexer_1_out, twos_complement_1_absolute_val, value_x;

  D_Flip_Flop d_ff_1 (.D(button), .clk(clock_1_out), .Q(init_reset));  // open: Qn, preset, reset
  Clock clock_1 (.out(clock_1_out));
  or or_1 (or_1_out, reset_t, init_reset);
  debouce debouce_1 (.button(init_reset), .debouced(play));
  debouce debouce_2 (.button(reset), .debouced(reset_t));
  accel_final_driver_v2 accel_final_driver_v2_1 (
    .rst(or_1_out), .miso(miso), .accel_input(accel_input), .enable_accel(1'b1), .x_offset(16'h3b),
    .y_offset(16'h3b), .z_offset(16'h3b), .mosi(mosi), .sclk(sclk), .cs(cs),
    .x_filtered(accel_final_driver_v2_1_x_filtered));  // open: y_filtered, z_filtered, left, down, right, up, x_small, y_small, x_medium, y_medium, x_large, y_large
  or or_2 (or_2_out, reset_t, init_reset);
  save_random_val save_random_val_1 (
    .min_value(8'h14), .max_value(8'h5f), .button(play), .reset(reset_t),
    .final_random_val(save_random_val_1_final_random_val));
  save_random_val save_random_val_2 (
    .min_value({8{1'b0}}), .max_value(8'h1), .button(play), .reset(reset_t),
    .final_random_val(save_random_val_2_final_random_val));
  Adder #(.width(16)) adder_1 (
    .a(value_x), .b(accel_final_driver_v2_1_x_filtered), .out(adder_1_out));  // open: cin, cout
  Comparator #(.width(16)) comparator_1 (.a(adder_1_out), .b({16{1'b0}}), .eq(comparator_1_eq));  // open: gt, lt
  Comparator #(.width(16)) comparator_2 (.a(adder_1_out), .b(16'h64), .eq(comparator_2_eq));  // open: gt, lt
  Clock #(.highDuration(2), .lowDuration(2)) clock_2 (.out(clock_2_out));
  Comparator #(.width(16)) comparator_3 (.a(adder_1_out), .b(16'hff9c), .eq(comparator_3_eq));  // open: gt, lt
  D_Flip_Flop d_ff_2 (.Q(d_ff_2_q), .preset(debouce_3_debouced), .reset(or_2_out));  // open: D, clk, Qn
  debouce debouce_3 (.button(play), .debouced(debouce_3_debouced));
  D_Flip_Flop d_ff_3 (.D(or_3_out), .clk(clock_2_out), .Q(d_ff_3_q));  // open: Qn, preset, reset
  or or_3 (or_3_out, comparator_1_eq, comparator_2_eq, comparator_3_eq);
  absolute_val_and_sign absolute_val_and_sign_1 (
    .unfiltered(adder_1_out), .value(absolute_val_and_sign_1_value),
    .negative(absolute_val_and_sign_1_negative));
  and and_1 (and_1_out, d_ff_3_q, d_ff_2_q);
  D_Flip_Flop d_ff_4 (.Q(done), .preset(and_1_out), .reset(or_2_out));  // open: D, clk, Qn
  twos_complement twos_complement_1 (
    .negative_number({{8{1'b0}}, save_random_val_1_final_random_val}),
    .absolute_val(twos_complement_1_absolute_val));
  Multiplexer #(.width(16)) multiplexer_1 (
    .in0(absolute_val_and_sign_1_value), .in1({16{1'b0}}), .out(multiplexer_1_out), .sel(done));
  Multiplexer #(.width(16)) multiplexer_2 (
    .in0({{8{1'b0}}, save_random_val_1_final_random_val}), .in1(twos_complement_1_absolute_val),
    .out(value_x), .sel(save_random_val_2_final_random_val[0]));
  hex_to_decimal_16_bits hex_to_decimal_16_bits_1 (
    .val(multiplexer_1_out), .tens(hex_to_decimal_16_bits_1_tens), .ones(hex_to_decimal_16_bits_1_ones));  // open: hundreds
  sign_hex_output sign (.negative(absolute_val_and_sign_1_negative));
  sevenseg_numbers_output hex1 (.input_bus(hex_to_decimal_16_bits_1_tens));  // open: decimal
  sevenseg_numbers_output hex0 (.input_bus(hex_to_decimal_16_bits_1_ones));  // open: decimal
endmodule

module pseudo_random (
  input  [7:0] min_value,
  input  [7:0] max_value,
  input  enable,
  input  reset,
  output [7:0] random_val
);

  wire clock_1_out, comparator_1_gt, comparator_2_lt, or_1_out;
  wire [7:0] counter_1_q;

  Clock clock_1 (.out(clock_1_out));
  Counter counter_1 (
    .load(or_1_out), .up(1'b1), .count(1'b1), .clk(clock_1_out), .D(min_value), .Q(counter_1_q));  // open: clr, carry
  Comparator #(.mode("unsigned")) comparator_1 (.a(counter_1_q), .b(max_value), .gt(comparator_1_gt));  // open: eq, lt
  Comparator #(.mode("unsigned")) comparator_2 (.a(counter_1_q), .b(min_value), .lt(comparator_2_lt));  // open: gt, eq
  Register register_1 (.D(counter_1_q), .en(enable), .clk(clock_1_out), .Q(random_val), .clr(reset));
  or or_1 (or_1_out, comparator_1_gt, comparator_2_lt);
endmodule

module random_val_tb (
  input  button,
  input  reset
);

  wire absolute_val_and_sign_1_negative, debouce_1_debouced, debouce_2_debouced;
  wire [3:0] hex_to_decimal_16_bits_1_hundreds, hex_to_decimal_16_bits_1_ones, hex_to_decimal_16_bits_1_tens;
  wire [7:0] save_random_val_1_final_random_val, save_random_val_2_final_random_val;
  wire [15:0] absolute_val_and_sign_1_value, twos_complement_1_absolute_val, value;

  debouce debouce_1 (.button(button), .debouced(debouce_1_debouced));
  debouce debouce_2 (.button(reset), .debouced(debouce_2_debouced));
  save_random_val save_random_val_1 (
    .min_value(8'h14), .max_value(8'h5f), .button(debouce_1_debouced), .reset(debouce_2_debouced),
    .final_random_val(save_random_val_1_final_random_val));
  save_random_val save_random_val_2 (
    .min_value({8{1'b0}}), .max_value(8'h1), .button(debouce_1_debouced), .reset(debouce_2_debouced),
    .final_random_val(save_random_val_2_final_random_val));
  Multiplexer #(.width(16)) multiplexer_1 (
    .in0({{8{1'b0}}, save_random_val_1_final_random_val}), .in1(twos_complement_1_absolute_val), .out(value),
    .sel(save_random_val_2_final_random_val[0]));
  twos_complement twos_complement_1 (
    .negative_number({{8{1'b0}}, save_random_val_1_final_random_val}),
    .absolute_val(twos_complement_1_absolute_val));
  absolute_val_and_sign absolute_val_and_sign_1 (
    .unfiltered(value), .value(absolute_val_and_sign_1_value), .negative(absolute_val_and_sign_1_negative));
  hex_to_decimal_16_bits hex_to_decimal_16_bits_1 (
    .val(absolute_val_and_sign_1_value), .hundreds(hex_to_decimal_16_bits_1_hundreds),
    .tens(hex_to_decimal_16_bits_1_tens), .ones(hex_to_decimal_16_bits_1_ones));
  sign_hex_output hex3 (.negative(absolute_val_and_sign_1_negative));
  sevenseg_numbers_output hex2 (.input_bus(hex_to_decimal_16_bits_1_hundreds));  // open: decimal
  sevenseg_numbers_output hex1 (.input_bus(hex_to_decimal_16_bits_1_tens));  // open: decimal
  sevenseg_numbers_output hex0 (.input_bus(hex_to_decimal_16_bits_1_ones));  // open: decimal
endmodule

module save_random_val (
  input  [7:0] min_value,
  input  [7:0] max_value,
  input  button,
  input  reset,
  output [7:0] final_random_val
);

  wire clock_1_out, not_1_out;
  wire [7:0] pseudo_random_1_random_val;

  not not_1 (not_1_out, button);
  pseudo_random pseudo_random_1 (
    .min_value(min_value), .max_value(max_value), .enable(not_1_out), .reset(reset),
    .random_val(pseudo_random_1_random_val));
  Register register_1 (
    .D(pseudo_random_1_random_val), .en(button), .clk(clock_1_out), .Q(final_random_val), .clr(reset));
  Clock clock_1 (.out(clock_1_out));
endmodule

module debouce (
  input  button,
  output debouced
);

  wire clock_1_out;

  Clock #(.highDuration(2), .lowDuration(2)) clock_1 (.out(clock_1_out));
  D_Flip_Flop d_ff_1 (.D(button), .clk(clock_1_out), .Q(debouced));  // open: Qn, preset, reset
endmodule

module letters_logic (
  input  [4:0] letter,
  output [6:0] letter_out
);

  wire and_1_out, and_2_out, and_3_out, and_4_out, and_5_out, and_6_out, and_7_out, and_8_out, and_9_out,
       and_10_out, and_11_out, and_12_out, and_13_out, and_14_out, and_15_out, and_16_out, and_17_out,
       and_18_out, and_19_out, and_20_out, and_21_out, and_22_out, and_23_out, and_24_out, and_25_out,
       and_26_out, and_27_out, and_28_out, and_29_out, and_30_out, and_31_out, and_32_out, and_33_out,
       and_34_out, and_35_out, and_36_out, and_37_out, and_38_out, and_39_out, and_40_out, and_41_out,
       and_42_out, and_43_out, and_44_out, and_45_out, and_46_out, and_47_out, and_48_out, and_49_out,
       and_50_out, and_51_out, and_52_out, and_53_out, and_54_out, and_55_out, and_56_out, not_1_out,
       not_2_out, not_3_out, not_4_out, not_5_out;

  not not_1 (not_1_out, letter[4]);
  not not_2 (not_2_out, letter[3]);
  not not_3 (not_3_out, letter[2]);
  not not_4 (not_4_out, letter[1]);
  not not_5 (not_5_out, letter[0]);
  and and_1 (and_1_out, not_1_out, not_2_out, not_4_out, letter[0]);
  and and_2 (and_2_out, not_1_out, not_2_out, letter[1], not_5_out);
  and and_3 (and_3_out, not_1_out, not_2_out, letter[2]);
  and and_4 (and_4_out, not_1_out, letter[2], letter[1]);
  and and_5 (and_5_out, letter[3], not_3_out, not_4_out, not_5_out);
  and and_6 (and_6_out, not_1_out, letter[3], letter[1], letter[0]);
  and and_7 (and_7_out, letter[4], not_2_out, not_3_out);
  and and_8 (and_8_out, letter[4], not_2_out, not_4_out, not_5_out);
  and and_9 (and_9_out, letter[4], not_3_out, not_4_out);
  and and_10 (and_10_out, letter[4], not_3_out, not_5_out);
  and and_11 (and_11_out, not_1_out, not_3_out, letter[0]);
  and and_12 (and_12_out, not_1_out, not_4_out, letter[0]);
  and and_13 (and_13_out, not_2_out, not_3_out, letter[0]);
  and and_14 (and_14_out, not_3_out, not_4_out, letter[0]);
  and and_15 (and_15_out, not_1_out, not_2_out, letter[1]);
  and and_16 (and_16_out, not_1_out, letter[3], not_4_out);
  and and_17 (and_17_out, letter[4], not_2_out, not_4_out);
  and and_18 (and_18_out, letter[4], not_3_out, not_4_out);
  and and_19 (and_19_out, not_1_out, not_3_out, letter[0]);
  and and_20 (and_20_out, not_2_out, letter[1], not_5_out);
  and and_21 (and_21_out, not_1_out, letter[2], not_5_out);
  and and_22 (and_22_out, not_2_out, letter[2], not_4_out);
  and and_23 (and_23_out, not_1_out, letter[3], not_4_out);
  and and_24 (and_24_out, not_1_out, letter[3], letter[0]);
  and and_25 (and_25_out, letter[4], not_3_out, not_5_out);
  and and_26 (and_26_out, not_1_out, not_2_out, not_3_out, letter[1]);
  and and_27 (and_27_out, not_1_out, not_2_out, letter[1], letter[0]);
  and and_28 (and_28_out, not_2_out, not_3_out, letter[1], letter[0]);
  and and_29 (and_29_out, not_1_out, letter[2], not_4_out, not_5_out);
  and and_30 (and_30_out, not_2_out, letter[2], not_4_out);
  and and_31 (and_31_out, not_1_out, letter[2], letter[1], letter[0]);
  and and_32 (and_32_out, letter[3], not_3_out, letter[1], not_5_out);
  and and_33 (and_33_out, letter[4], not_2_out, letter[2], not_5_out);
  and and_34 (and_34_out, not_2_out, not_3_out, not_4_out, letter[0]);
  and and_35 (and_35_out, not_1_out, not_3_out, letter[1], not_5_out);
  and and_36 (and_36_out, not_1_out, not_2_out, letter[2], not_4_out, not_5_out);
  and and_37 (and_37_out, not_1_out, letter[2], letter[1], letter[0]);
  and and_38 (and_38_out, letter[3], not_3_out, not_4_out, not_5_out);
  and and_39 (and_39_out, not_1_out, letter[3], letter[1], not_5_out);
  and and_40 (and_40_out, not_1_out, letter[3], letter[2], letter[0]);
  and and_41 (and_41_out, letter[4], not_2_out, not_3_out, letter[0]);
  and and_42 (and_42_out, letter[4], not_2_out, not_4_out, letter[0]);
  and and_43 (and_43_out, letter[4], not_2_out, letter[2], letter[1], not_5_out);
  and and_44 (and_44_out, letter[4], letter[3], not_3_out, not_4_out);
  and and_45 (and_45_out, not_2_out, not_3_out, not_4_out, letter[0]);
  and and_46 (and_46_out, not_1_out, not_2_out, letter[2], not_4_out, not_5_out);
  and and_47 (and_47_out, not_1_out, not_2_out, letter[2], letter[1], letter[0]);
  and and_48 (and_48_out, letter[3], not_3_out, not_5_out);
  and and_49 (and_49_out, not_1_out, letter[3], letter[2], not_4_out, letter[0]);
  and and_50 (and_50_out, letter[4], not_3_out, not_4_out);
  and and_51 (and_51_out, letter[4], not_2_out, not_4_out, letter[0]);
  and and_52 (and_52_out, not_2_out, not_3_out, letter[0]);
  and and_53 (and_53_out, not_1_out, letter[2], not_4_out, letter[0]);
  and and_54 (and_54_out, not_1_out, not_2_out, letter[2], letter[1]);
  and and_55 (and_55_out, letter[4], not_2_out, not_3_out, not_4_out);
  and and_56 (and_56_out, letter[4], letter[3], not_3_out, letter[1], not_5_out);
  or or_1 (letter_out[6], and_1_out, and_2_out, and_3_out, and_4_out, and_5_out, and_6_out, and_7_out, and_8_out, and_9_out, and_10_out);
  or or_2 (letter_out[5], and_11_out, and_12_out, and_13_out, and_14_out, and_15_out, and_16_out, and_17_out, and_18_out);
  or or_3 (letter_out[4], and_19_out, and_20_out, and_21_out, and_22_out, and_23_out, and_24_out, and_25_out);
  or or_4 (letter_out[3], and_26_out, and_27_out, and_28_out, and_29_out, and_30_out, and_31_out, and_32_out, and_33_out);
  or or_5 (letter_out[2], and_34_out, and_35_out, and_36_out, and_37_out, and_38_out, and_39_out, and_40_out, and_41_out, and_42_out, and_43_out, and_44_out);
  or or_6 (letter_out[1], and_45_out, and_46_out, and_47_out, and_48_out, and_49_out, and_50_out, and_51_out);
  or or_7 (letter_out[0], and_52_out, and_53_out, and_54_out, and_55_out, and_56_out);
endmodule

module letter_no_decimal (
  input  [4:0] letter_num,
  output [7:0] no_dec_letter
);

  letters_logic letters_logic_1 (.letter(letter_num), .letter_out(no_dec_letter[6:0]));

  assign no_dec_letter[7] = 1'b0;
endmodule

module side_to_side_anim (
  input  clock,
  input  [7:0] hex5_letter,
  input  [7:0] hex4_letter,
  input  [7:0] hex3_letter,
  input  [7:0] hex2_letter,
  input  [7:0] hex1_letter,
  output [7:0] hex5_out,
  output [7:0] hex4_out,
  output [7:0] hex3_out,
  output [7:0] hex2_out,
  output [7:0] hex1_out,
  output [7:0] hex0_out
);

  Multiplexer #(.width(8)) multiplexer_1 (.in0(hex5_letter), .out(hex5_out), .sel(clock));  // open: in1
  Multiplexer #(.width(8)) multiplexer_2 (.in0(hex4_letter), .in1(hex5_letter), .out(hex4_out), .sel(clock));
  Multiplexer #(.width(8)) multiplexer_3 (.in0(hex3_letter), .in1(hex4_letter), .out(hex3_out), .sel(clock));
  Multiplexer #(.width(8)) multiplexer_4 (.in0(hex2_letter), .in1(hex3_letter), .out(hex2_out), .sel(clock));
  Multiplexer #(.width(8)) multiplexer_5 (.in0(hex1_letter), .in1(hex2_letter), .out(hex1_out), .sel(clock));
  Multiplexer #(.width(8)) multiplexer_6 (.in1(hex1_letter), .out(hex0_out), .sel(clock));  // open: in0
endmodule

module blink_anim (
  input  clock,
  input  [7:0] hex5_letter,
  input  [7:0] hex4_letter,
  input  [7:0] hex3_letter,
  input  [7:0] hex2_letter,
  input  [7:0] hex1_letter,
  input  [7:0] hex0_letter,
  output [7:0] hex5_out,
  output [7:0] hex4_out,
  output [7:0] hex3_out,
  output [7:0] hex2_out,
  output [7:0] hex1_out,
  output [7:0] hex0_out
);

  Multiplexer #(.width(8)) multiplexer_1 (.in0(hex5_letter), .out(hex5_out), .sel(clock));  // open: in1
  Multiplexer #(.width(8)) multiplexer_2 (.in0(hex4_letter), .out(hex4_out), .sel(clock));  // open: in1
  Multiplexer #(.width(8)) multiplexer_3 (.in0(hex3_letter), .out(hex3_out), .sel(clock));  // open: in1
  Multiplexer #(.width(8)) multiplexer_4 (.in0(hex2_letter), .out(hex2_out), .sel(clock));  // open: in1
  Multiplexer #(.width(8)) multiplexer_5 (.in0(hex1_letter), .out(hex1_out), .sel(clock));  // open: in1
  Multiplexer #(.width(8)) multiplexer_6 (.in0(hex0_letter), .out(hex0_out), .sel(clock));  // open: in1
endmodule
