// Logisim project print_ADXL345_values.circ as structural Verilog: 9 circuits, main circuit print_accel_values_raw
module print_values_filtered_sim (
  input  _10__Z_AXIS
);

  wire clock_1_out, reset;
  wire [1:0] SELECTOR;
  wire [3:0] bit_extender_4_out, bit_extender_5_out, bit_extender_6_out;
  wire [7:0] hundreds, lowpass_filter_sim_1_p5, multiplexer_1_out, ones, scale_down_sim_1_answer, tens, x, y,
       z;
  wire [15:0] bit_extender_1_out, bit_extender_2_out;
  wire [31:0] bit_extender_3_out, hex_to_decimal_sim_1_hundreds, hex_to_decimal_sim_1_ones,
       hex_to_decimal_sim_1_tens;

  DipSwitch #(.number(2)) AXIS_SELECTOR (.sw1(SELECTOR[0]), .sw2(SELECTOR[1]));
  Slider slider_1 (.out(x));
  Slider slider_2 (.out(y));
  Slider slider_3 (.out(z));
  Multiplexer #(.select(2), .width(8)) multiplexer_1 (
    .in0(x), .in1(y), .in2(z), .out(multiplexer_1_out), .sel(SELECTOR));  // open: in3
  assign bit_extender_1_out = {{8{1'b0}}, multiplexer_1_out};  // Bit_Extender bit_extender_1
  scale_down_sim scale_down_sim_1 (
    .number_input(bit_extender_1_out), .second_num(32'h3200), .answer(scale_down_sim_1_answer));  // open: negative, hundreds, tens, ones
  assign bit_extender_2_out = {{8{1'b0}}, scale_down_sim_1_answer};  // Bit_Extender bit_extender_2
  _7_Segment_Display u_7_segment_display_1 (.g(_10__Z_AXIS));  // open: f, a, b, e, d, c, dp
  Clock clock_1 (.out(clock_1_out));
  _7_Segment_Display u_7_segment_display_2 (
    .g(hundreds[6]), .f(hundreds[5]), .a(hundreds[0]), .b(hundreds[1]), .e(hundreds[4]), .d(hundreds[3]),
    .c(hundreds[2]), .dp(1'b1));
  _7_Segment_Display u_7_segment_display_3 (
    .g(tens[6]), .f(tens[5]), .a(tens[0]), .b(tens[1]), .e(tens[4]), .d(tens[3]), .c(tens[2]));  // open: dp
  _7_Segment_Display u_7_segment_display_4 (
    .g(ones[6]), .f(ones[5]), .a(ones[0]), .b(ones[1]), .e(ones[4]), .d(ones[3]), .c(ones[2]));  // open: dp
  // lowpass_filter_sim lowpass_filter_sim_1: pin names not known; wires that end beside it: bit_extender_2_out, clock_1_out, reset, reset, lowpass_filter_sim_1_p5
  hex_to_decimal_sim hex_to_decimal_sim_1 (
    .input_num(bit_extender_3_out), .hundreds(hex_to_decimal_sim_1_hundreds),
    .tens(hex_to_decimal_sim_1_tens), .ones(hex_to_decimal_sim_1_ones));
  assign bit_extender_3_out = {{24{1'b0}}, lowpass_filter_sim_1_p5};  // Bit_Extender bit_extender_3
  Bit_Extender #(.in_width(32), .out_width(4)) bit_extender_4 (
    .in(hex_to_decimal_sim_1_hundreds), .out(bit_extender_4_out));
  Bit_Extender #(.in_width(32), .out_width(4)) bit_extender_5 (
    .in(hex_to_decimal_sim_1_tens), .out(bit_extender_5_out));
  Bit_Extender #(.in_width(32), .out_width(4)) bit_extender_6 (
    .in(hex_to_decimal_sim_1_ones), .out(bit_extender_6_out));
  sevenseg_accel_logic sevenseg_accel_logic_1 (.accel(bit_extender_4_out), .sevensegment(hundreds));
  sevenseg_accel_logic sevenseg_accel_logic_2 (.accel(bit_extender_5_out), .sevensegment(tens));
  sevenseg_accel_logic sevenseg_accel_logic_3 (.accel(bit_extender_6_out), .sevensegment(ones));

  // Other names for the same wires on the sheet: negative = _10__Z_AXIS

  // Notes on the sheet:
  //   PRINT_ADXL345_VALUES
  //   00: X-AXIS
  //   01: Y-AXIS
  //   THE "AXES_SELECTOR" ALLOWS US TO SWITCH BETWEEN THE DIFFERENT AXES
  //   OUTPUTS ON 4 HEXES THE VALUES OF THE ACCELERATION ON THE DIFFERENT AXES OF THE ACCELEROMETER
endmodule

module print_values_filtered (
  input  rst,
  input  miso,
  input  accel_input,
  input  enable_accel,
  output mosi,
  output sclk,
  output cs
);

  wire clock_1_out, scale_down_1_negative;
  wire [1:0] SELECTOR;
  wire [3:0] hex_to_decimal_1_hundreds, hex_to_decimal_1_ones, hex_to_decimal_1_tens, scale_down_1_hundreds,
       scale_down_1_ones, scale_down_1_tens;
  wire [7:0] lowpass_filter_de10_1_filtered;
  wire [15:0] multiplexer_1_out, scale_down_1_answer, subtractor_1_out, subtractor_2_out, subtractor_3_out,
       x, y, z;

  DipSwitch #(.number(2)) AXIS_SELECTOR (.sw1(SELECTOR[0]), .sw2(SELECTOR[1]));
  Subtractor #(.width(16)) subtractor_1 (.a(x), .b(16'h3b), .out(subtractor_1_out));  // open: bin, bout
  Subtractor #(.width(16)) subtractor_2 (.a(y), .b(16'h3b), .out(subtractor_2_out));  // open: bin, bout
  Subtractor #(.width(16)) subtractor_3 (.a(z), .b(16'h3b), .out(subtractor_3_out));  // open: bin, bout
  Multiplexer #(.select(2), .width(16)) multiplexer_1 (
    .in0(subtractor_1_out), .in1(subtractor_2_out), .in2(subtractor_3_out), .out(multiplexer_1_out),
    .sel(SELECTOR));  // open: in3
  accel_main_driver accel_main_driver_1 (
    .rst(rst), .miso(miso), .accel_input(accel_input), .enable_accel(enable_accel), .mosi(mosi), .sclk(sclk),
    .cs(cs), .Accelerometer({z, y, x}));
  scale_down scale_down_1 (
    .number_input(multiplexer_1_out), .second_num(16'h6400), .negative(scale_down_1_negative),
    .hundreds(scale_down_1_hundreds), .tens(scale_down_1_tens), .ones(scale_down_1_ones),
    .answer(scale_down_1_answer));
  Clock #(.highDuration(1562500), .lowDuration(1562500)) clock_1 (.out(clock_1_out));
  hex_to_decimal hex_to_decimal_1 (
    .val(lowpass_filter_de10_1_filtered), .hundreds(hex_to_decimal_1_hundreds), .tens(hex_to_decimal_1_tens),
    .ones(hex_to_decimal_1_ones));
  lowpass_filter_de10 lowpass_filter_de10_1 (
    .negative(scale_down_1_negative), .unfiltered(scale_down_1_answer), .clock(clock_1_out), .reset(rst),
    .filtered(lowpass_filter_de10_1_filtered));  // open: negative_val
  sevenseg_accel_output HEX1 (.Input_bus_1(scale_down_1_hundreds), .decimal(1'b1));
  sevenseg_accel_output HEX2 (.Input_bus_1(scale_down_1_tens));  // open: decimal
  sevenseg_accel_output HEX3 (.Input_bus_1(scale_down_1_ones));  // open: decimal
  sevenseg_accel_output HEX4 (.Input_bus_1(hex_to_decimal_1_hundreds), .decimal(1'b1));
  sevenseg_accel_output HEX5 (.Input_bus_1(hex_to_decimal_1_tens));  // open: decimal
  sevenseg_accel_output HEX6 (.Input_bus_1(hex_to_decimal_1_ones));  // open: decimal

  // Other names for the same wires on the sheet: reset = rst

  // Notes on the sheet:
  //   PRINT_ADXL345_VALUES
  //   00: X-AXIS
  //   01: Y-AXIS
  //   10: Z-AXIS
  //   THE "AXES_SELECTOR" ALLOWS US TO SWITCH BETWEEN THE DIFFERENT AXES
  //   OUTPUTS ON 4 HEXES THE VALUES OF THE ACCELERATION ON THE DIFFERENT AXES OF THE ACCELEROMETER
endmodule

module print_accel_values_raw (
  input  rst,
  input  miso,
  input  accel_input,
  input  enable_accel,
  output mosi,
  output sclk,
  output cs
);

  wire [1:0] SELECTOR;
  wire [3:0] multiplexer_1_out, multiplexer_2_out, multiplexer_3_out, multiplexer_4_out;
  wire [47:0] accel_main_driver_1_accelerometer;

  DipSwitch #(.number(2)) AXIS_SELECTOR (.sw1(SELECTOR[0]), .sw2(SELECTOR[1]));
  accel_main_driver accel_main_driver_1 (
    .rst(rst), .miso(miso), .accel_input(accel_input), .enable_accel(enable_accel), .mosi(mosi), .sclk(sclk),
    .cs(cs), .Accelerometer(accel_main_driver_1_accelerometer));
  Multiplexer #(.select(2), .width(4)) multiplexer_1 (
    .in0(accel_main_driver_1_accelerometer[3:0]), .in1(accel_main_driver_1_accelerometer[19:16]),
    .in2(accel_main_driver_1_accelerometer[35:32]), .out(multiplexer_1_out), .sel(SELECTOR));  // open: in3
  sevenseg_accel_output HEX0 (.Input_bus_1(multiplexer_1_out));  // open: decimal
  Multiplexer #(.select(2), .width(4)) multiplexer_2 (
    .in0(accel_main_driver_1_accelerometer[7:4]), .in1(accel_main_driver_1_accelerometer[23:20]),
    .in2(accel_main_driver_1_accelerometer[39:36]), .out(multiplexer_2_out), .sel(SELECTOR));  // open: in3
  sevenseg_accel_output HEX1 (.Input_bus_1(multiplexer_2_out));  // open: decimal
  Multiplexer #(.select(2), .width(4)) multiplexer_3 (
    .in0(accel_main_driver_1_accelerometer[11:8]), .in1(accel_main_driver_1_accelerometer[27:24]),
    .in2(accel_main_driver_1_accelerometer[43:40]), .out(multiplexer_3_out), .sel(SELECTOR));  // open: in3
  sevenseg_accel_output HEX2 (.Input_bus_1(multiplexer_3_out));  // open: decimal
  Multiplexer #(.select(2), .width(4)) multiplexer_4 (
    .in0(accel_main_driver_1_accelerometer[15:12]), .in1(accel_main_driver_1_accelerometer[31:28]),
    .in2(accel_main_driver_1_accelerometer[47:44]), .out(multiplexer_4_out), .sel(SELECTOR));  // open: in3
  sevenseg_accel_output HEX3 (.Input_bus_1(multiplexer_4_out));  // open: decimal

  // Notes on the sheet:
  //   PRINT_ADXL345_VALUES
  //   00: X-AXIS
  //   01: Y-AXIS
  //   10: Z-AXIS
  //   THE "AXES_SELECTOR" ALLOWS US TO SWITCH BETWEEN THE DIFFERENT AXES
  //   OUTPUTS ON 4 HEXES THE VALUES OF THE ACCELERATION ON THE DIFFERENT AXES OF THE ACCELEROMETER
endmodule

module sevenseg_accel_logic (
  input  [3:0] accel,
  output [7:0] sevensegment
);

  wire and_1_out, and_2_out, and_3_out, and_4_out, and_5_out, and_6_out, and_7_out, and_8_out, and_9_out,
       and_10_out, and_11_out, and_12_out, and_13_out, and_14_out, and_15_out, and_16_out, and_17_out,
       and_18_out, and_19_out, and_20_out, and_21_out, and_22_out, and_23_out, and_24_out, and_25_out,
       and_26_out, and_27_out, and_28_out, and_29_out, and_30_out, and_31_out, and_32_out, and_33_out,
       and_34_out, and_35_out, and_36_out, not_1_out, not_2_out, not_3_out, not_4_out;

  not not_1 (not_1_out, accel[3]);
  not not_2 (not_2_out, accel[2]);
  not not_3 (not_3_out, accel[1]);
  not not_4 (not_4_out, accel[0]);
  and and_1 (and_1_out, not_2_out, accel[1]);
  and and_2 (and_2_out, accel[1], not_4_out);
  and and_3 (and_3_out, not_1_out, accel[2], not_3_out);
  and and_4 (and_4_out, accel[3], not_2_out);
  and and_5 (and_5_out, accel[3], accel[0]);
  and and_6 (and_6_out, not_3_out, not_4_out);
  and and_7 (and_7_out, not_1_out, accel[2], not_3_out);
  and and_8 (and_8_out, accel[2], not_4_out);
  and and_9 (and_9_out, accel[3], not_2_out);
  and and_10 (and_10_out, accel[3], accel[1]);
  and and_11 (and_11_out, not_2_out, not_4_out);
  and and_12 (and_12_out, accel[1], not_4_out);
  and and_13 (and_13_out, accel[3], accel[1]);
  and and_14 (and_14_out, accel[3], accel[2]);
  and and_15 (and_15_out, not_1_out, not_2_out, not_4_out);
  and and_16 (and_16_out, not_1_out, accel[1], not_4_out);
  and and_17 (and_17_out, not_2_out, accel[1], accel[0]);
  and and_18 (and_18_out, accel[2], not_3_out, accel[0]);
  and and_19 (and_19_out, accel[3], not_3_out);
  and and_20 (and_20_out, accel[3], accel[2], not_4_out);
  and and_21 (and_21_out, not_1_out, not_3_out);
  and and_22 (and_22_out, not_1_out, accel[0]);
  and and_23 (and_23_out, not_3_out, accel[0]);
  and and_24 (and_24_out, not_1_out, accel[2]);
  and and_25 (and_25_out, accel[3], not_2_out);
  and and_26 (and_26_out, not_1_out, not_2_out);
  and and_27 (and_27_out, not_1_out, not_3_out, not_4_out);
  and and_28 (and_28_out, not_2_out, not_4_out);
  and and_29 (and_29_out, not_1_out, accel[1], accel[0]);
  and and_30 (and_30_out, accel[3], not_3_out, accel[0]);
  and and_31 (and_31_out, not_2_out, not_4_out);
  and and_32 (and_32_out, not_1_out, accel[1]);
  and and_33 (and_33_out, not_1_out, accel[2], accel[0]);
  and and_34 (and_34_out, accel[2], accel[1]);
  and and_35 (and_35_out, accel[3], not_2_out, not_3_out);
  and and_36 (and_36_out, accel[3], not_4_out);
  or or_1 (sevensegment[6], and_1_out, and_2_out, and_3_out, and_4_out, and_5_out);
  or or_2 (sevensegment[5], and_6_out, and_7_out, and_8_out, and_9_out, and_10_out);
  or or_3 (sevensegment[4], and_11_out, and_12_out, and_13_out, and_14_out);
  or or_4 (sevensegment[3], and_15_out, and_16_out, and_17_out, and_18_out, and_19_out, and_20_out);
  or or_5 (sevensegment[2], and_21_out, and_22_out, and_23_out, and_24_out, and_25_out);
  or or_6 (sevensegment[1], and_26_out, and_27_out, and_28_out, and_29_out, and_30_out);
  or or_7 (sevensegment[0], and_31_out, and_32_out, and_33_out, and_34_out, and_35_out, and_36_out);

  assign sevensegment[7] = 1'b0;
endmodule

module sevenseg_accel_output (
  input  [3:0] Input_bus_1,
  input  decimal
);

  wire [7:0] sevenseg_1_sevensegment;

  sevenseg_accel_logic sevenseg_1 (.accel(Input_bus_1), .sevensegment(sevenseg_1_sevensegment));
  _7_Segment_Display L_7_Segment_Display_1 (
    .g(sevenseg_1_sevensegment[6]), .f(sevenseg_1_sevensegment[5]), .a(sevenseg_1_sevensegment[0]),
    .b(sevenseg_1_sevensegment[1]), .e(sevenseg_1_sevensegment[4]), .d(sevenseg_1_sevensegment[3]),
    .c(sevenseg_1_sevensegment[2]), .dp(decimal));
endmodule

module converting_to_right_range (
  input  [15:0] raw_accel_value,
  output [3:0] hundreds,
  output [3:0] tens,
  output [3:0] ones
);

  wire [7:0] divider_1_out, divider_1_rem;
  wire [15:0] fptoint_1_p2;
  wire [31:0] bit_extender_1_out, fpdivider_1_out, fpmultiplier_1_out;

  assign bit_extender_1_out = {{16{raw_accel_value[15]}}, raw_accel_value};  // Bit_Extender bit_extender_1
  // Probe on bit_extender_1_out
  FPDivider fpdivider_1 (.a(bit_extender_1_out), .b(32'h100), .out(fpdivider_1_out));
  // Probe on fpdivider_1_out
  // Probe on fpmultiplier_1_out
  FPMultiplier fpmultiplier_1 (.a(fpdivider_1_out), .b(32'h42c80000), .out(fpmultiplier_1_out));
  // FPToInt #(.mode("truncate"), .width(16)) fptoint_1: pin names not known; wires that end beside it: fpmultiplier_1_out, fptoint_1_p2
  // Probe on fptoint_1_p2
  Bit_Extender #(.out_width(4), .\type ("zero")) bit_extender_2 (.in(divider_1_out), .out(hundreds));
  Divider divider_1 (
    .a(fptoint_1_p2[7:0]), .b(8'h64), .out(divider_1_out), .upper(fptoint_1_p2[15:8]), .rem(divider_1_rem));
  // Probe on divider_1_rem
  Divider #(.width(4)) divider_2 (
    .a(divider_1_rem[3:0]), .b(4'b1010), .out(tens), .upper(divider_1_rem[7:4]), .rem(ones));

  // Notes on the sheet:
  //   divided by 256
  //   times 100
  //   divided by 100
  //   divided by 10
endmodule

module lowpass_filter_sim (
  input  [15:0] unfiltered,
  input  clock,
  input  reset,
  input  [7:0] in_4,
  input  [7:0] in_5,
  output [7:0] filtered_val,
  output [7:0] out_7
);

  wire not_1_out, not_2_out;
  wire [15:0] adder_2_out, adder_3_out, adder_4_out, adder_5_out, out1, out2, out3, out4, out5;

  Register #(.width(16)) register_1 (.D(unfiltered), .en(1'b1), .clk(clock), .Q(out1), .clr(reset));
  Adder adder_1 (.a(in_4), .b(in_5), .out(out_7));  // open: cin, cout
  Adder #(.width(16)) adder_2 (.a(out1), .b(out2), .out(adder_2_out));  // open: cin, cout
  Adder #(.width(16)) adder_3 (.a(adder_2_out), .b(out3), .out(adder_3_out));  // open: cin, cout
  Register #(.width(16)) register_2 (.D(out1), .en(1'b1), .clk(not_1_out), .Q(out2), .clr(reset));
  not not_1 (not_1_out, clock);
  Adder #(.width(16)) adder_4 (.a(adder_3_out), .b(out4), .out(adder_4_out));  // open: cin, cout
  Adder #(.width(16)) adder_5 (.a(adder_4_out), .b(out5), .out(adder_5_out));  // open: cin, cout
  Register #(.width(16)) register_3 (.D(out2), .en(1'b1), .clk(clock), .Q(out3), .clr(reset));
  Divider divider_1 (.a(adder_5_out[7:0]), .b(8'h5), .out(filtered_val), .upper(adder_5_out[15:8]));  // open: rem
  Register #(.width(16)) register_4 (.D(out3), .en(1'b1), .clk(not_2_out), .Q(out4), .clr(reset));
  not not_2 (not_2_out, clock);
  Register #(.width(16)) register_5 (.D(out4), .en(1'b1), .clk(clock), .Q(out5), .clr(reset));
endmodule

module lowpass_filter_de10 (
  input  negative,
  input  [15:0] unfiltered,
  input  clock,
  input  reset,
  output negative_val,
  output [7:0] filtered
);

  wire not_1_out, not_2_out, not_3_out, not_4_out;
  wire [7:0] multiplexer_2_out;
  wire [14:0] adder_8_out;
  wire [15:0] adder_1_out, adder_2_out, adder_3_out, adder_4_out, adder_5_out, adder_6_out, adder_7_out,
       adder_9_out, divide_two_num_1_final_answer_sixteen_bits, out1, out2, out3, out4, out5, out6, out7,
       out8, out9, out10, twos_complement_1_absolute_val, twos_complement_2_absolute_val, value;

  Register #(.width(16)) register_1 (.D(value), .en(1'b1), .clk(clock), .Q(out1), .clr(reset));
  Register #(.width(16)) register_2 (.D(out5), .en(1'b1), .clk(clock), .Q(out6), .clr(reset));
  Adder #(.width(16)) adder_1 (.a(out1), .b(out2), .out(adder_1_out));  // open: cin, cout
  Adder #(.width(16)) adder_2 (.a(adder_9_out), .b(out7), .out(adder_2_out));  // open: cin, cout
  twos_complement twos_complement_1 (.negative_number(unfiltered), .absolute_val(twos_complement_1_absolute_val));
  Register #(.width(16)) register_3 (.D(out1), .en(1'b1), .clk(not_1_out), .Q(out2), .clr(reset));
  not not_1 (not_1_out, clock);
  Register #(.width(16)) register_4 (.D(out6), .en(1'b1), .clk(not_2_out), .Q(out7), .clr(reset));
  not not_2 (not_2_out, clock);
  Adder #(.width(16)) adder_3 (.a(adder_1_out), .b(out3), .out(adder_3_out));  // open: cin, cout
  Adder #(.width(16)) adder_4 (.a(adder_2_out), .b(out8), .out(adder_4_out));  // open: cin, cout
  Multiplexer #(.width(16)) multiplexer_1 (
    .in0(unfiltered), .in1(twos_complement_1_absolute_val), .out(value), .sel(negative));
  Adder #(.width(16)) adder_5 (.a(adder_3_out), .b(out4), .out(adder_5_out));  // open: cin, cout
  Adder #(.width(16)) adder_6 (.a(adder_4_out), .b(out9), .out(adder_6_out));  // open: cin, cout
  divide_two_num divide_two_num_1 (
    .val({negative_val, adder_8_out}), .val2(16'hccd),
    .final_answer_sixteen_bits(divide_two_num_1_final_answer_sixteen_bits));  // open: final_answer
  Register #(.width(16)) register_5 (.D(out2), .en(1'b1), .clk(clock), .Q(out3), .clr(reset));
  Register #(.width(16)) register_6 (.D(out7), .en(1'b1), .clk(clock), .Q(out8), .clr(reset));
  Adder #(.width(16)) adder_7 (.a(adder_5_out), .b(out5), .out(adder_7_out));  // open: cin, cout
  Adder #(.width(16)) adder_8 (.a(adder_6_out), .b(out10), .out({negative_val, adder_8_out}));  // open: cin, cout
  twos_complement twos_complement_2 (
    .negative_number(divide_two_num_1_final_answer_sixteen_bits),
    .absolute_val(twos_complement_2_absolute_val));
  Adder #(.width(16)) adder_9 (.a(adder_7_out), .b(out6), .out(adder_9_out));  // open: cin, cout
  Register #(.width(16)) register_7 (.D(out3), .en(1'b1), .clk(not_3_out), .Q(out4), .clr(reset));
  not not_3 (not_3_out, clock);
  Register #(.width(16)) register_8 (.D(out8), .en(1'b1), .clk(not_4_out), .Q(out9), .clr(reset));
  not not_4 (not_4_out, clock);
  Multiplexer #(.width(16)) multiplexer_2 (
    .in0(divide_two_num_1_final_answer_sixteen_bits), .in1(twos_complement_2_absolute_val),
    .out({multiplexer_2_out, filtered}), .sel(negative_val));
  Register #(.width(16)) register_9 (.D(out4), .en(1'b1), .clk(clock), .Q(out5), .clr(reset));
  Register #(.width(16)) register_10 (.D(out9), .en(1'b1), .clk(clock), .Q(out10), .clr(reset));

  // Other names for the same wires on the sheet: final_sign = negative_val
endmodule

module filtered_test (
  input  Input_1
);

  wire clock_1_out;
  wire [7:0] DipSwitch_1_sw1, lowpass_filter_de10_1_p1, lowpass_filter_de10_1_p4;

  DipSwitch DipSwitch_1 (
    .sw1(DipSwitch_1_sw1[0]), .sw2(DipSwitch_1_sw1[1]), .sw3(DipSwitch_1_sw1[2]), .sw4(DipSwitch_1_sw1[3]),
    .sw5(DipSwitch_1_sw1[4]), .sw6(DipSwitch_1_sw1[5]), .sw7(DipSwitch_1_sw1[6]), .sw8(DipSwitch_1_sw1[7]));
  Clock clock_1 (.out(clock_1_out));
  // lowpass_filter_de10 lowpass_filter_de10_1: pin names not known; wires that end beside it: {lowpass_filter_de10_1_p1, DipSwitch_1_sw1}, clock_1_out, Input_1, lowpass_filter_de10_1_p4
  sevenseg_accel_output sevenseg_accel_output_1 (.Input_bus_1(lowpass_filter_de10_1_p4[3:0]));  // open: decimal
  sevenseg_accel_output sevenseg_accel_output_2 (.Input_bus_1(lowpass_filter_de10_1_p4[7:4]));  // open: decimal
endmodule
