// Logisim project Application.circ as structural Verilog: 6 circuits, main circuit main
module main (
);

  // driver driver_1: pin names not known
endmodule

module letter8_reader (
  input  [63:0] saved_message,
  input  write_done,
  input  clk,
  input  reset,
  output [7:0] output_letter,
  output update_disp
);

  wire comparator_1_eq, not_1_out, or_1_out;
  wire [3:0] letter_count_q;
  wire [21:0] slow_clock_q;

  not not_1 (not_1_out, write_done);
  or or_1 (or_1_out, not_1_out, reset);
  Counter #(.max('h1312d0), .width(22)) slow_clock (
    .clr(or_1_out), .load(1'b0), .up(1'b1), .count(1'b1), .clk(clk), .D(22'h1312d0), .Q(slow_clock_q));  // open: carry
  Comparator #(.mode("unsigned"), .width(22)) comparator_1 (
    .a(slow_clock_q), .b(22'h1312d0), .eq(comparator_1_eq));  // open: gt, lt
  and and_1 (update_disp, write_done, comparator_1_eq);
  Counter #(.max('h8), .width(4)) letter_count (
    .clr(reset), .load(1'b0), .up(1'b1), .count(1'b1), .clk(update_disp), .D(4'b1000), .Q(letter_count_q));  // open: carry
  Multiplexer #(.select(4), .width(8)) multiplexer_1 (
    .in0({8{1'b0}}), .in1(saved_message[7:0]), .in2(saved_message[15:8]), .in3(saved_message[23:16]),
    .in4(saved_message[31:24]), .in5(saved_message[39:32]), .in6(saved_message[47:40]),
    .in7(saved_message[55:48]), .in8(saved_message[63:56]), .in9({8{1'b0}}), .in10({8{1'b0}}),
    .in11({8{1'b0}}), .in12({8{1'b0}}), .in13({8{1'b0}}), .in14({8{1'b0}}), .in15({8{1'b0}}),
    .out(output_letter), .sel(letter_count_q));
endmodule

module sentence_disp (
  input  [7:0] newletter,
  input  enable,
  input  clk,
  input  reset,
  output [7:0] letter0,
  output [7:0] letter1,
  output [7:0] letter2,
  output [7:0] letter3,
  output [7:0] letter4,
  output [7:0] letter5
);

  Register register_1 (.D(newletter), .en(enable), .clk(clk), .Q(letter0), .clr(reset));
  Register register_2 (.D(letter0), .en(enable), .clk(clk), .Q(letter1), .clr(reset));
  Register register_3 (.D(letter1), .en(enable), .clk(clk), .Q(letter2), .clr(reset));
  Register register_4 (.D(letter2), .en(enable), .clk(clk), .Q(letter3), .clr(reset));
  Register register_5 (.D(letter3), .en(enable), .clk(clk), .Q(letter4), .clr(reset));
  Register register_6 (.D(letter4), .en(enable), .clk(clk), .Q(letter5), .clr(reset));
endmodule

module bin_to_seg (
  input  [7:0] ascii_in,
  output [7:0] seg_out
);

  wire and_1_out, and_2_out, and_3_out, and_4_out, and_5_out, and_6_out, and_7_out, and_8_out, and_9_out,
       and_10_out, and_11_out, and_12_out, and_13_out, and_14_out, and_15_out, and_16_out, and_17_out,
       and_18_out, and_19_out, and_20_out, and_21_out, and_22_out, and_23_out, and_24_out, and_25_out,
       and_26_out, and_27_out, and_28_out, and_29_out, and_30_out, and_31_out, and_32_out, and_33_out,
       and_34_out, and_35_out, and_36_out, and_37_out, and_38_out, and_39_out, and_40_out, and_41_out,
       and_42_out, and_43_out, and_44_out, and_45_out, and_46_out, and_47_out, and_48_out, and_49_out,
       and_50_out, and_51_out, and_52_out, and_53_out, and_54_out, and_55_out, and_56_out, and_57_out,
       and_58_out, and_59_out, and_60_out, and_61_out, and_62_out, and_63_out, and_64_out, and_65_out,
       and_66_out, and_67_out, and_68_out, and_69_out, and_70_out, and_71_out, and_72_out, and_73_out,
       and_74_out, and_75_out, and_76_out, and_77_out, and_78_out, and_79_out, and_80_out, not_1_out,
       not_2_out, not_3_out, not_4_out, not_5_out, not_6_out, not_7_out, not_8_out;

  not not_1 (not_1_out, ascii_in[7]);
  not not_2 (not_2_out, ascii_in[6]);
  not not_3 (not_3_out, ascii_in[5]);
  not not_4 (not_4_out, ascii_in[4]);
  not not_5 (not_5_out, ascii_in[3]);
  not not_6 (not_6_out, ascii_in[2]);
  not not_7 (not_7_out, ascii_in[1]);
  not not_8 (not_8_out, ascii_in[0]);
  and and_1 (and_1_out, not_1_out, not_2_out, not_3_out, not_4_out, not_5_out, not_6_out, not_7_out, not_8_out);
  and and_2 (and_2_out, not_1_out, not_2_out, ascii_in[5], not_4_out, not_5_out, not_6_out, not_7_out, ascii_in[0]);
  and and_3 (and_3_out, not_1_out, not_2_out, ascii_in[5], not_4_out, ascii_in[3], ascii_in[2], ascii_in[1], not_8_out);
  and and_4 (and_4_out, not_1_out, ascii_in[6], not_4_out, ascii_in[3], not_6_out, ascii_in[1], ascii_in[0]);
  and and_5 (and_5_out, ascii_in[7], ascii_in[6], ascii_in[5], ascii_in[4], ascii_in[3], ascii_in[2], ascii_in[1], ascii_in[0]);
  and and_6 (and_6_out, not_1_out, ascii_in[6], not_4_out, not_5_out, not_7_out, ascii_in[0]);
  and and_7 (and_7_out, not_1_out, ascii_in[6], not_4_out, not_5_out, ascii_in[1], not_8_out);
  and and_8 (and_8_out, not_1_out, ascii_in[6], not_5_out, ascii_in[2], not_7_out, not_8_out);
  and and_9 (and_9_out, not_1_out, ascii_in[6], not_4_out, ascii_in[2], ascii_in[1], not_8_out);
  and and_10 (and_10_out, not_1_out, ascii_in[6], not_4_out, ascii_in[3], not_6_out, not_7_out, not_8_out);
  and and_11 (and_11_out, not_1_out, ascii_in[6], not_4_out, ascii_in[3], not_6_out, ascii_in[1], ascii_in[0]);
  and and_12 (and_12_out, not_1_out, ascii_in[6], ascii_in[4], not_5_out, not_6_out);
  and and_13 (and_13_out, not_1_out, ascii_in[6], ascii_in[4], not_6_out, not_7_out, ascii_in[0]);
  and and_14 (and_14_out, not_1_out, ascii_in[6], ascii_in[4], not_6_out, ascii_in[1], not_8_out);
  and and_15 (and_15_out, not_1_out, ascii_in[6], ascii_in[5], not_5_out, not_6_out, ascii_in[0]);
  and and_16 (and_16_out, not_1_out, ascii_in[6], ascii_in[5], not_4_out, ascii_in[1], ascii_in[0]);
  and and_17 (and_17_out, ascii_in[7], ascii_in[6], ascii_in[5], ascii_in[4], ascii_in[3], ascii_in[2], ascii_in[1], ascii_in[0]);
  and and_18 (and_18_out, not_1_out, ascii_in[6], not_5_out, not_7_out, ascii_in[0]);
  and and_19 (and_19_out, not_1_out, ascii_in[6], not_3_out, not_4_out, not_5_out, ascii_in[1]);
  and and_20 (and_20_out, not_1_out, ascii_in[6], not_4_out, not_5_out, ascii_in[1], not_8_out);
  and and_21 (and_21_out, not_1_out, ascii_in[6], not_3_out, not_4_out, ascii_in[2], ascii_in[0]);
  and and_22 (and_22_out, not_1_out, ascii_in[6], not_4_out, not_5_out, ascii_in[2], ascii_in[1]);
  and and_23 (and_23_out, not_1_out, ascii_in[6], not_4_out, ascii_in[3], not_7_out, not_8_out);
  and and_24 (and_24_out, not_1_out, ascii_in[6], not_4_out, ascii_in[3], not_6_out, ascii_in[1], ascii_in[0]);
  and and_25 (and_25_out, not_1_out, ascii_in[6], not_4_out, ascii_in[3], ascii_in[2], not_7_out);
  and and_26 (and_26_out, not_1_out, ascii_in[6], ascii_in[4], not_5_out, not_7_out);
  and and_27 (and_27_out, not_1_out, ascii_in[6], ascii_in[4], not_6_out, not_7_out);
  and and_28 (and_28_out, not_1_out, ascii_in[6], ascii_in[4], not_5_out, not_6_out, ascii_in[0]);
  and and_29 (and_29_out, ascii_in[7], ascii_in[6], ascii_in[5], ascii_in[4], ascii_in[3], ascii_in[2], ascii_in[1], ascii_in[0]);
  and and_30 (and_30_out, not_1_out, ascii_in[6], not_3_out, not_4_out, ascii_in[0]);
  and and_31 (and_31_out, not_1_out, ascii_in[6], not_4_out, not_6_out, ascii_in[0]);
  and and_32 (and_32_out, not_1_out, ascii_in[6], not_5_out, ascii_in[1], not_8_out);
  and and_33 (and_33_out, not_1_out, ascii_in[6], not_5_out, ascii_in[2], not_7_out);
  and and_34 (and_34_out, not_1_out, ascii_in[6], not_4_out, ascii_in[3], not_7_out);
  and and_35 (and_35_out, not_1_out, ascii_in[6], not_4_out, ascii_in[3], ascii_in[2]);
  and and_36 (and_36_out, not_1_out, ascii_in[6], ascii_in[4], not_6_out, not_8_out);
  and and_37 (and_37_out, not_1_out, ascii_in[6], ascii_in[4], not_5_out, ascii_in[2]);
  and and_38 (and_38_out, ascii_in[7], ascii_in[6], ascii_in[5], ascii_in[4], ascii_in[3], ascii_in[2], ascii_in[1], ascii_in[0]);
  and and_39 (and_39_out, not_1_out, not_3_out, not_4_out, ascii_in[3], not_6_out, ascii_in[1], not_8_out);
  and and_40 (and_40_out, not_1_out, ascii_in[6], not_4_out, not_5_out, not_6_out, ascii_in[1]);
  and and_41 (and_41_out, not_1_out, ascii_in[6], not_5_out, ascii_in[1], ascii_in[0]);
  and and_42 (and_42_out, not_1_out, ascii_in[6], not_3_out, not_4_out, ascii_in[2], not_7_out, not_8_out);
  and and_43 (and_43_out, not_1_out, ascii_in[6], not_4_out, not_5_out, ascii_in[2], not_7_out);
  and and_44 (and_44_out, not_1_out, ascii_in[6], not_5_out, ascii_in[2], ascii_in[0]);
  and and_45 (and_45_out, not_1_out, ascii_in[6], not_4_out, ascii_in[2], ascii_in[1], ascii_in[0]);
  and and_46 (and_46_out, not_1_out, ascii_in[6], ascii_in[3], not_6_out, ascii_in[1], not_8_out);
  and and_47 (and_47_out, ascii_in[7], ascii_in[6], ascii_in[5], ascii_in[4], ascii_in[3], ascii_in[2], ascii_in[1], ascii_in[0]);
  and and_48 (and_48_out, not_1_out, ascii_in[6], not_5_out, not_6_out, not_7_out, ascii_in[0]);
  and and_49 (and_49_out, not_1_out, ascii_in[6], not_4_out, not_6_out, ascii_in[1], not_8_out);
  and and_50 (and_50_out, not_1_out, ascii_in[6], not_4_out, not_5_out, ascii_in[2], not_7_out, not_8_out);
  and and_51 (and_51_out, not_1_out, ascii_in[6], not_4_out, ascii_in[2], ascii_in[1], ascii_in[0]);
  and and_52 (and_52_out, not_1_out, ascii_in[6], ascii_in[3], not_6_out, not_7_out, not_8_out);
  and and_53 (and_53_out, not_1_out, ascii_in[6], not_4_out, ascii_in[3], ascii_in[1], not_8_out);
  and and_54 (and_54_out, not_1_out, ascii_in[6], not_4_out, ascii_in[3], ascii_in[2], ascii_in[0]);
  and and_55 (and_55_out, not_1_out, ascii_in[6], ascii_in[4], not_5_out, ascii_in[0]);
  and and_56 (and_56_out, not_1_out, ascii_in[6], ascii_in[4], not_5_out, ascii_in[2], ascii_in[1]);
  and and_57 (and_57_out, not_1_out, ascii_in[6], ascii_in[4], ascii_in[3], not_6_out, not_7_out);
  and and_58 (and_58_out, ascii_in[7], ascii_in[6], ascii_in[5], ascii_in[4], ascii_in[3], ascii_in[2], ascii_in[1], ascii_in[0]);
  and and_59 (and_59_out, not_1_out, not_3_out, not_4_out, ascii_in[3], not_6_out, ascii_in[1], not_8_out);
  and and_60 (and_60_out, not_1_out, ascii_in[5], not_4_out, not_5_out, not_6_out, not_7_out, ascii_in[0]);
  and and_61 (and_61_out, not_1_out, ascii_in[6], not_5_out, not_6_out, not_7_out, ascii_in[0]);
  and and_62 (and_62_out, not_1_out, ascii_in[6], not_4_out, not_5_out, ascii_in[2], not_7_out, not_8_out);
  and and_63 (and_63_out, not_1_out, ascii_in[6], not_3_out, ascii_in[3], not_6_out, not_8_out);
  and and_64 (and_64_out, not_1_out, ascii_in[6], not_4_out, ascii_in[3], not_6_out, ascii_in[1]);
  and and_65 (and_65_out, not_1_out, ascii_in[6], not_3_out, not_4_out, ascii_in[3], ascii_in[2], ascii_in[0]);
  and and_66 (and_66_out, not_1_out, ascii_in[6], not_4_out, ascii_in[3], ascii_in[2], not_7_out, ascii_in[0]);
  and and_67 (and_67_out, not_1_out, ascii_in[6], ascii_in[4], not_6_out, not_7_out);
  and and_68 (and_68_out, not_1_out, ascii_in[6], ascii_in[4], not_5_out, not_7_out, ascii_in[0]);
  and and_69 (and_69_out, not_1_out, ascii_in[6], ascii_in[4], ascii_in[3], not_6_out, not_8_out);
  and and_70 (and_70_out, not_1_out, ascii_in[6], ascii_in[5], not_4_out, not_5_out, ascii_in[2], ascii_in[1], ascii_in[0]);
  and and_71 (and_71_out, ascii_in[7], ascii_in[6], ascii_in[5], ascii_in[4], ascii_in[3], ascii_in[2], ascii_in[1], ascii_in[0]);
  and and_72 (and_72_out, not_1_out, ascii_in[6], not_3_out, not_5_out, not_6_out, ascii_in[0]);
  and and_73 (and_73_out, not_1_out, ascii_in[6], not_5_out, not_6_out, not_7_out, ascii_in[0]);
  and and_74 (and_74_out, not_1_out, ascii_in[6], not_3_out, not_4_out, ascii_in[2], ascii_in[0]);
  and and_75 (and_75_out, not_1_out, ascii_in[6], not_4_out, ascii_in[2], not_7_out, ascii_in[0]);
  and and_76 (and_76_out, not_1_out, ascii_in[6], not_4_out, not_5_out, ascii_in[2], ascii_in[1]);
  and and_77 (and_77_out, not_1_out, ascii_in[6], ascii_in[4], not_5_out, not_6_out, not_7_out);
  and and_78 (and_78_out, not_1_out, ascii_in[6], ascii_in[4], not_5_out, not_6_out, ascii_in[0]);
  and and_79 (and_79_out, not_1_out, ascii_in[6], ascii_in[4], ascii_in[3], not_6_out, ascii_in[1], not_8_out);
  and and_80 (and_80_out, ascii_in[7], ascii_in[6], ascii_in[5], ascii_in[4], ascii_in[3], ascii_in[2], ascii_in[1], ascii_in[0]);
  or or_1 (seg_out[7], and_1_out, and_2_out, and_3_out, and_4_out, and_5_out);
  or or_2 (seg_out[6], and_6_out, and_7_out, and_8_out, and_9_out, and_10_out, and_11_out, and_12_out, and_13_out, and_14_out, and_15_out, and_16_out, and_17_out);
  or or_3 (seg_out[5], and_18_out, and_19_out, and_20_out, and_21_out, and_22_out, and_23_out, and_24_out, and_25_out, and_26_out, and_27_out, and_28_out, and_29_out);
  or or_4 (seg_out[4], and_30_out, and_31_out, and_32_out, and_33_out, and_34_out, and_35_out, and_36_out, and_37_out, and_38_out);
  or or_5 (seg_out[3], and_39_out, and_40_out, and_41_out, and_42_out, and_43_out, and_44_out, and_45_out, and_46_out, and_47_out);
  or or_6 (seg_out[2], and_48_out, and_49_out, and_50_out, and_51_out, and_52_out, and_53_out, and_54_out, and_55_out, and_56_out, and_57_out, and_58_out);
  or or_7 (seg_out[1], and_59_out, and_60_out, and_61_out, and_62_out, and_63_out, and_64_out, and_65_out, and_66_out, and_67_out, and_68_out, and_69_out, and_70_out, and_71_out);
  or or_8 (seg_out[0], and_72_out, and_73_out, and_74_out, and_75_out, and_76_out, and_77_out, and_78_out, and_79_out, and_80_out);
endmodule

module rx_display (
  input  [63:0] message,
  input  disp_ready,
  input  clk,
  input  reset,
  output [7:0] seg0,
  output [7:0] seg1,
  output [7:0] seg2,
  output [7:0] seg3,
  output [7:0] seg4,
  output [7:0] seg5
);

  wire letter8_reader_1_update_disp;
  wire [7:0] bin_to_seg_1_seg_out, letter8_reader_1_output_letter;

  letter8_reader letter8_reader_1 (
    .saved_message(message), .write_done(disp_ready), .clk(clk), .reset(reset),
    .output_letter(letter8_reader_1_output_letter), .update_disp(letter8_reader_1_update_disp));
  bin_to_seg bin_to_seg_1 (.ascii_in(letter8_reader_1_output_letter), .seg_out(bin_to_seg_1_seg_out));
  sentence_disp sentence_disp_1 (
    .newletter(bin_to_seg_1_seg_out), .enable(letter8_reader_1_update_disp), .clk(clk), .reset(reset),
    .letter0(seg0), .letter1(seg1), .letter2(seg2), .letter3(seg3), .letter4(seg4), .letter5(seg5));
endmodule

module fsm (
  input  cycle_button,
  input  select_button,
  input  [1:0] main_selector,
  input  message_selector,
  input  select_pressed,
  output [2:0] final_output,
  output select_pressed1,
  output [1:0] main_selector1,
  output message_selector1
);
endmodule
