// Logisim project uart_tx.circ as structural Verilog: 1 circuit, main circuit main
module main (
  input  Run_test,
  output letter_output,
  output Serial_n_out,
  output [7:0] letter
);

  wire clock_1_out, uart_tx_1_p2;

  Clock clock_1 (.out(clock_1_out));
  // VHDL_Entity #(.content("library IEEE;\nuse IEEE.STD_LOGIC_1164.ALL;\nuse IEEE.NUMERIC_STD.ALL;\n\nentity uart_tx_tester is\n    Port (\n        clk_50M : in STD_LOGIC;               -- Input clock, assumed 50 MHz\n        run_test_raw : in STD_LOGIC;          -- HIGH indicates to continuously run test\n        tx_busy : in STD_LOGIC;               -- HIGH indicates transmitter is busy \n        data_out : out STD_LOGIC_VECTOR (7 downto 0);  -- Data byte (8 bits) to transmit\n        trigger : out STD_LOGIC                -- Trigger to tell UART module to begin transmission\n    );\nend uart_tx_tester;\n\narchitecture Behavioral of uart_tx_tester is\n\n    signal run_test_0 : std_logic := '0';          -- Synchronizer for 'start test' switch input\n    signal run_test : std_logic := '0';            -- Synchronizer for 'start test' switch input\n    signal tester_state : unsigned(5 downto 0) := (others => '0');  -- FSM state variable\n    -- signal byte_index : unsigned(31 downto 0) := unsigned(8*16)-unsigned(1);          -- Pointer to beginning of next byte to transmit in 16 byte message\n    constant BYTE_INDEX_INIT: natural := (8*16)-1; -- Calculate the initial value for byte_index\n    signal byte_index : unsigned(31 downto 0) := to_unsigned(BYTE_INDEX_INIT, 32); -- Initialize byte_index with the calculated value\n	 signal pause_delay : unsigned(31 downto 0) := (others => '0');  -- Counter for delay between re-transmissions of message\n    signal trigger_ctr : unsigned(5 downto 0) := (others => '0');    -- Delay to hold trigger high, in clock cycles\n\n    constant STATE_IDLE : unsigned(5 downto 0) := \"000000\";          -- Legal values for tester_state\n    constant STATE_LOAD : unsigned(5 downto 0) := \"000010\";          -- Legal values for tester_state\n    constant STATE_TRIGGER : unsigned(5 downto 0) := \"000100\";       -- Legal values for tester_state\n    constant STATE_POLL_BUSY : unsigned(5 downto 0) := \"001000\";     -- Legal values for tester_state\n    constant STATE_PAUSE : unsigned(5 downto 0) := \"010000\";         -- Legal values for tester_state\n\n    constant MSG_DELAY : unsigned(31 downto 0) := to_unsigned(100_000_000, 32);  -- Delay between messages re-transmissions, in clk cycles\n	 \n	 -- Message to transmit\n    signal byte_str : std_logic_vector((8*16)-1 downto 0) := \"01001000\" & \"01100101\" & \"01101100\" & \"01101100\" & \"01101111\" & \"00100000\" & \"01010111\" & \"01101111\" &\n                                                             \"01110010\" & \"01101100\" & \"01100100\" & \"00100001\" & \"00100000\" & \"00100000\" & \"00100000\" & \"00100000\";\n-- hello world! is \"01001000\" & \"01100101\" & \"01101100\" & \"01101100\" & \"01101111\" & \"00100000\" & \"01010111\" & \"01101111\" &\n                                                            -- \"01110010\" & \"01101100\" & \"01100100\" & \"00100001\" & \"00100000\" & \"00100000\" & \"00100000\" & \"00100000\";\n\n\nbegin\n\n    -- Synchronizer for \"run_test\" input since, as tested, this comes from a \n    -- slide switch on the DE10-Lite board, which is not synchronous with the\n    -- clock.\n    process (clk_50M) begin\n        if rising_edge(clk_50M) then\n            run_test_0 <= run_test_raw;\n            run_test <= run_test_0;\n        end if;\n    end process;\n\n    -- Main Finite State Machine that sequences the test\n    process (clk_50M) begin\n        if rising_edge(clk_50M) then\n            case tester_state is\n                -- Wait for request to begin test.\n                when STATE_IDLE =>\n                    trigger <= '0';\n                    if run_test = '1' then\n                        byte_index <= to_unsigned(BYTE_INDEX_INIT, 32);\n                        tester_state <= STATE_LOAD;\n                    end if;\n                    \n                -- Output next byte to transmitter module, with trigger still low\n                -- so it won't transmit yet.\n                when STATE_LOAD =>\n                    trigger <= '0';\n                    data_out <= byte_str(to_integer(byte_index) downto to_integer(byte_index)-7);\n                    trigger_ctr <= to_unsigned(5, 6);\n                    tester_state <= STATE_TRIGGER;\n                    \n                -- Now that previous state output'd the next byte to transmit,\n                -- assert the trigger signal to begin the transmission.\n                when STATE_TRIGGER =>\n                    trigger <= '1';\n                    trigger_ctr <= trigger_ctr - 1;\n                    if trigger_ctr = 0 then\n                        tester_state <= STATE_POLL_BUSY;\n                    end if;\n                    \n                -- Clear trigger signal, and wait until all bits shifted out\n                -- for the current byte.\n                when STATE_POLL_BUSY =>\n                    trigger <= '0';\n                    if tx_busy = '0' then\n                        if byte_index <= 7 then\n                            pause_delay <= (others => '0');\n                            tester_state <= STATE_PAUSE;\n                        else\n                            byte_index <= byte_index - 8;\n                            tester_state <= STATE_LOAD;\n                        end if;\n                    end if;\n                    \n                -- Once transmitted full message, pause before \n                -- transmitting message again for testing convenience.\n                when STATE_PAUSE =>\n                    pause_delay <= pause_delay + 1;\n                    if pause_delay > to_integer(MSG_DELAY) then\n                        tester_state <= STATE_IDLE;\n                    end if;\n                    \n                -- Should never get here, but if do, return to IDLE\n                when others =>\n                    tester_state <= STATE_IDLE;\n            end case;\n        end if;\n    end process;\n\nend Behavioral;")) uart_tx_tester_1: pin names not known; wires that end beside it: clock_1_out, Run_test, letter_output
  // VHDL_Entity #(.content("library IEEE;\nuse IEEE.STD_LOGIC_1164.ALL;\nuse IEEE.NUMERIC_STD.ALL;\n\nentity uart_tx is\n    Port (\n        clk_50M : in STD_LOGIC;               -- Input clock, assumed 50 MHz\n        data_raw : in STD_LOGIC_VECTOR (7 downto 0);  -- Data byte (8 bits) to transmit\n        trigger_raw : in STD_LOGIC;           -- Tells module to begin transmission of data_raw byte\n        busy : out STD_LOGIC;                 -- Flag to indicate a transmission is in progress\n        serial_out : out STD_LOGIC            -- UART output serial datastream\n    );\nend uart_tx;\n\narchitecture Behavioral of uart_tx is\n	 \n	 constant CLKS_PER_BIT: integer := 8680; -- normally 868, reduce it to 1 for simulations\n	 \n    type state_type is (STATE_IDLE, STATE_TRANSMITTING, STATE_CLEANUP);\n    signal tx_state : state_type := STATE_IDLE;  -- State variable for main finite state machine\n    signal data_aug : std_logic_vector(9 downto 0) := (others => '0');  -- Augmented data word to transmit that includes START bit, data byte, and STOP BIT\n    signal tx_index : unsigned(3 downto 0) := (others => '0');  -- Index of bit currently transmitting\n    signal bit_delay : unsigned(31 downto 0) := (others => '0'); -- Timer to regulate baud rate\n\n    signal trigger_0 : std_logic := '0';  -- Synchronizer on trigger input signal\n    signal trigger : std_logic := '0';    -- Synchronizer on trigger input signal\n\n    -- Localparam CLKS_PER_BIT is not needed in VHDL since it's used as a constant value in the code directly\n\nbegin\n\n    process (clk_50M) begin\n        if rising_edge(clk_50M) then\n            case tx_state is\n                -- Wait for trigger condition indicating it's time to transmit a byte.\n                when STATE_IDLE =>\n                    busy <= '0';                 -- Indicate that transmitter is idle.\n                    serial_out <= '1';           -- Idle output HIGH, per standard UART behavior.\n                    if trigger = '1' then        -- Check if received trigger to TX a byte\n                        data_aug <= '1' & data_raw & '0';   -- Create augmented byte with start and stop bits\n                        busy <= '1';                        -- Indicate that transmitter is busy.\n                        bit_delay <= (others => '0');       -- Clear timer used to track duration of each bit\n                        tx_index <= (others => '0');        -- Point to first bit of data_aug to TX, namely the start bit\n                        tx_state <= STATE_TRANSMITTING;     -- Move on to next state\n                    end if;\n                    \n                -- Transmit all 10 bits with proper the proper duration per bit based on the selected baud rate.\n                when STATE_TRANSMITTING =>\n                    serial_out <= data_aug(to_integer(tx_index));  -- Set output based on current bit to transmit\n                    bit_delay <= bit_delay + 1;                     -- Keep track of duration to hold this bit\n                    if bit_delay > to_unsigned(CLKS_PER_BIT, 32) then  -- Check if bit duration has expired\n                        if tx_index = \"1001\" then                  -- Check if just transmitted the final bit, i.e. the STOP bit\n                            tx_state <= STATE_CLEANUP;            -- Move on to next state\n                        else\n                            tx_index <= tx_index + 1;             -- Still more bits to send so, point to next bit\n                            bit_delay <= (others => '0');         -- Clear counter used to regulate baud rate\n                        end if;\n                    end if;\n                    \n                -- Pause for a few bit durations after full byte transmitted.\n                when STATE_CLEANUP =>\n                    bit_delay <= bit_delay + 1;                    -- Keep track of how long been in cleanup state\n                    if bit_delay > to_unsigned(5 * CLKS_PER_BIT, 32) then  -- If paused HIGH long enough, then return to idle state\n                        tx_state <= STATE_IDLE;\n                    end if;\n                    \n                -- Should never get here, but if do, return to IDLE\n                when others =>\n                    tx_state <= STATE_IDLE;\n            end case;\n        end if;\n    end process;\n\n    -- Synchronizer for trigger input\n    process (clk_50M) begin\n        if rising_edge(clk_50M) then\n            trigger_0 <= trigger_raw;\n            trigger <= trigger_0;\n        end if;\n    end process;\n\nend Behavioral;")) uart_tx_1: pin names not known; wires that end beside it: letter, uart_tx_1_p2, clock_1_out, letter, uart_tx_1_p2, letter_output, Serial_n_out
endmodule
