// Logisim project test_Sr.circ as structural Verilog: 1 circuit, main circuit main
module main (
  input  in_1,
  input  in_2,
  output out_3,
  output out_4
);

  wire clock_1_out;

  Clock clock_1 (.out(clock_1_out));
  S_R_Flip_Flop s_r_ff_1 (.S(1'b0), .R(1'b0), .clk(clock_1_out), .Q(out_3), .reset(in_2), .Qn(out_4), .preset(in_1));
endmodule
